# Fritzing sketch flora_neopixel_binary_clock (saved by Fritzing 0.9.4)
breadboards: 1

parts:
  Part1 = Adafruit Flora [part_number="Adafruit #659"]
  NEOPIXEL1 = Neopixel Strip -- White (30/m) [part_number=1376]
  NEOPIXEL2 = Neopixel Strip -- White (30/m) [part_number=1376]
  NEOPIXEL3 = Neopixel Strip -- White (30/m) [part_number=1376]
  NEOPIXEL4 = Neopixel Strip -- White (30/m) [part_number=1376]
  NEOPIXEL5 = Neopixel Strip -- White (30/m) [part_number=1376]
  NEOPIXEL6 = Neopixel Strip -- White (30/m) [part_number=1376]
  Part2 = Adafruit DS3231 [part_number="Adafruit #3013"]

nets:
  +3V3: Part1.+3V3, Part2.Vin
  N1: Part1.IO6, NEOPIXEL1.Din
  GND: Part1.GND, NEOPIXEL1.GND, NEOPIXEL2.GND, NEOPIXEL3.GND, NEOPIXEL4.GND, NEOPIXEL5.GND, NEOPIXEL6.GND, Part2.GND
  N2: Part1.IO2/SDA, Part2.SCL
  N3: Part1.IO3/SCL, Part2.SDA
  +5V: Part1.VBAT, NEOPIXEL1.+5V, NEOPIXEL2.+5V, NEOPIXEL3.+5V, NEOPIXEL4.+5V, NEOPIXEL5.+5V, NEOPIXEL6.+5V
  N4: NEOPIXEL1.Dout, NEOPIXEL2.Din
  N5: NEOPIXEL2.Dout, NEOPIXEL3.Din
  N6: NEOPIXEL3.Dout, NEOPIXEL4.Din
  N7: NEOPIXEL4.Dout, NEOPIXEL5.Din
  N8: NEOPIXEL5.Dout, NEOPIXEL6.Din

notes:
  4x pixel strip
  Seconds 1s
  Bit:Pixel map:
  8 : 0
  4 : 1
  2 : 2
  1 : 3
  4x pixel strip
  Minutes 1s
  Bit:Pixel map:
  8 : 7
  4 : 8
  2 : 9
  1 : 10
  4x pixel strip
  Hours 1s
  Bit:Pixel map:
  8 : 14
  4 : 15
  2 : 16
  1 : 17
  3x pixel strip
  Seconds 10s
  Bit:Pixel map:
  4 : 6
  2 : 5
  1 : 4
  3x pixel strip
  Minutes 10s
  Bit:Pixel map:
  4 : 13
  2 : 12
  1 : 11
  2x pixel strip
  Hours 10s
  Bit:Pixel map:
  2 : 19
  1 : 18
  DS3231 Real Time Clock
  https://learn.adafruit.com/adafruit-ds3231-precision-rtc-breakout/overview
  CR1220 coin cell goes in the DS3231 for battery backup (keep time when powered off)
  MUST use Adafruit RTCLib http://github.com/adafruit/RTClib if using Adafruit's version
  Wire colour convention:
  Red: VCC
  Black: Ground
  Blue: Data
  Green: SDA
  Brown: SCL
  Neopixel strips, cut to length
  Adafruit Flora

custom parts:
  Adafruit Flora: FLORA is Adafruit's fully-featured wearable electronics platform. It's a round, sewable, Arduino-compatible microcontroller designed to empower amazing wearables projects. The FLORA is small (1.75" diameter, weighing 4.4 grams). The FLORA has built-in USB support. Built in USB means you plug it in to program it, it just shows up - all you need is a Micro-B USB cable, no additional purchases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
  Neopixel Strip -- White (30/m): These NeoPixel strips have 30 digitally-addressable pixel LEDs per meter and are very affordable and are only 12.5 mm wide, 10 mm if you remove the strip from the casing.
  Adafruit DS3231: The datasheet for the DS3231 explains that this part is an "Extremely Accurate I²C-Integrated RTC/TCXO/Crystal". And, hey, it does exactly what it says on the tin! This Real Time Clock (RTC) is the most precise you can get in a small, low power package. Most RTCs use an external 32kHz timing crystal that is used to keep time with low current draw. And that's all well and good, but those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
